# Fritzing sketch ocb (saved by Fritzing 0.9.3b)
breadboards: 3

parts:
  Componente1 = Arduino Mega 2560 (Rev3)
  ZS-042_RTC1 = ZS-042 RTC Module
  DS3 = DS18B20 1-Wire Temperature Sensor [part_number=DS18B20]
  R2 = Resistor [tolerance=±5% resistance=4.7k package=THT]
  U3 = Nextion Display [part_number=NX8048T070_011 package=Nextion_LCD]
  DS4 = DS18B20 1-Wire Temperature Sensor Probe Cable
  R3 = Resistor [tolerance=±5% resistance=4.7k package=THT]
  Power_plug1 = Power plug
  U4 = LM2596 step down module  # not connected
  Componente2 = Voltage Sensor 25V
  RE1 = KY-040 Rotary encoder [package=THT]
  Componente5 = Digital FM Radio Receiver
  SPKR1 = Loudspeaker
  RE2 = Rotary Encoder [package=THT]
  Componente6 = Mini Amplificador - OEP30WX2 - de Som Estéreo 2 Canais 30W + 30W
  U5 = Processamento de Audio - PT2314 [package=dil06]

nets:
  N1: Componente1.A2, RE2.EncoderPinB
  N2: Componente1.A3, RE2.EncoderPinA
  N3: Componente1.A4, Componente2.S
  N4: Componente1.A6, RE1.SW
  N5: Componente1.D21/SCL, Componente1.SCL, ZS-042_RTC1.SCL, Componente5.SCLK, U5.SCL
  N6: Componente1.D20/SDA, Componente1.SDA, ZS-042_RTC1.SDA, Componente5.SDIO, U5.SDA
  N7: Componente1.D17_PWM/RX2, U3.TX
  N8: Componente1.D16_PWM/TX2, U3.RX
  N9: Componente1.D15/RX3, RE1.CLK
  N10: Componente1.D14/TX3, RE1.DT
  N11: Componente1.D9_PWM, DS4.DQ, R3.Pin_1
  N12: Componente1.D8_PWM, DS3.DQ, R2.Pin_1
  3V3: Componente1.3V3, ZS-042_RTC1.VCC, Componente5.3.3V
  GND: Componente1.GND, ZS-042_RTC1.GND, DS3.GND, U3.GND, DS4.GND, Componente2.-, RE1.GND, Componente5.GND, RE2.EncoderPinC, Componente6.GND, Componente6.AGND, U5.GND
  VCC: Componente1.VIN, Componente6.VCC, U5.VCC
  VDD: Componente1.5V, DS3.VDD, R2.Pin_0, U3.+5v, DS4.VDD, R3.Pin_0, RE1.Vcc
  N13: Componente1.D52, Componente5.!RST
  GND_2: Power_plug1.GND, Componente2.GND
  VCC_2: Power_plug1.VCC, Componente2.VCC, Componente2.+
  N14: SPKR1.pin1, Componente6.SPR-
  N15: SPKR1.pin2, Componente6.SPR+
  N16: Componente6.INL, U5.L
  N17: Componente6.INR, U5.R

custom parts:
  Nextion Display: Nextion NX8048T070_011 Display TFT Display
  LM2596 step down module: LM2596 DC-DC step down power supply module 3 A.
  KY-040 Rotary encoder: KY-040 Rotary Encoder with switch on breakout borad from AZ Delivery
  Digital FM Radio Receiver: Description: This is a breakout board for the Silicon Laboratories Si4703 FM tuner chip. Beyond being a simple FM radio, the Si4703 is also capable of detecting and processing both Radio Data Service (RDS) and Radio Broadcast Data Service (RBDS) information. The Si4703 even does a very good job of filtering and carrier detection. It also enables data such as the station ID and song name to be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
  Mini Amplificador - OEP30WX2 - de Som Estéreo 2 Canais 30W + 30W: Description: A Placa Amplificador de Som 30W + 30W Estéreo é um circuito completo e ideal para quem necessita de um amplificador compacto e eficiente. De fácil instalação, conta com uma utilização mínima de componentes para melhorar as reproduções junto ao amplificador. É um módulo muito utilizado por hobistas e profissionais que necessitam de um equipamento amplificador que converta o sinal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
  Processamento de Audio - PT2314: Módulo de ajuste de qualidade de som - PT2314 Introdução do produto 1. Chip de processador de qualidade de som PT2314 integrado 2. O módulo suporta quatro conjuntos de entradas estéreo e saída de dois canais 3. O módulo suporta ajuste de volume, ajuste de agudos e graves, mudo e outras funções 4. O módulo suporta I2C ônibus para realizar todas as funções do programa 5. Luz indicadora de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
