# Fritzing sketch ocb_nextion (saved by Fritzing 0.9.3b)
circuit board: 10.1776cm x 5.36194cm
breadboards: 4

parts:
  Componente1 = Arduino Mega 2560 (Rev3)
  U1 = LM2596 step down module
  Power_plug1 = Power plug
  Componente2 = Voltage Sensor 25V
  DFPlayer_Mini1 = DFPlayer MINI [package="DIP (Dual Inline) [THT]"]
  Componente3 = Digital FM Radio Receiver
  R1 = Resistor [tolerance=±5% resistance=1k package=THT]
  RE1 = KY-040 Rotary encoder [package=THT]
  RE2 = Rotary Encoder [package=THT]
  DS1 = DS18B20 1-Wire Temperature Sensor [part_number=DS18B20]
  R2 = Resistor [tolerance=±5% resistance=4.7k package=THT]
  R3 = Resistor [tolerance=±5% resistance=4.7k package=THT]
  DS2 = DS18B20 1-Wire Temperature Sensor Probe Cable
  Componente4 = Mini Amplificador - OEP30WX2 - de Som Estéreo 2 Canais 30W + 30W
  U3 = Processamento de Audio - PT2314 [package=dil06]
  SP1 = SPEAKER [package=pcb_mount_speaker]
  BUTTON1 = Waterproof Pushbutton (blue)  # not connected
  ZS-042_RTC1 = ZS-042 RTC Module
  U2 = Nextion Display [part_number=NX8048T070_011 package=Nextion_LCD]

nets:
  N1: Componente1.A2, RE2.EncoderPinB
  N2: Componente1.A3, RE2.EncoderPinA
  N3: Componente1.A4, Componente2.S
  N4: Componente1.A6, RE1.SW
  N5: Componente1.D21/SCL, Componente1.SCL, Componente3.SDIO, U3.SDA, ZS-042_RTC1.SCL
  N6: Componente1.D20/SDA, Componente1.SDA, Componente3.SCLK, DS2.shield, U3.SCL, ZS-042_RTC1.SDA
  N7: Componente1.D19/RX1, RE1.CLK
  N8: Componente1.D18/TX1, RE1.DT
  N9: Componente1.D17_PWM/RX2, U2.TX
  N10: Componente1.D16_PWM/TX2, U2.RX
  N11: Componente1.D15/RX3, DFPlayer_Mini1.TX
  N12: Componente1.D14/TX3, R1.Pin_0
  N13: Componente1.D9_PWM, R3.Pin_1, DS2.DQ
  N14: Componente1.D8_PWM, DS1.DQ, R2.Pin_1
  3V3: Componente1.3V3, Componente3.3.3V, ZS-042_RTC1.VCC
  GND: Componente1.GND, U1.IN-, U1.OUT-, Power_plug1.GND, Componente2.GND, Componente2.-, DFPlayer_Mini1.GND, Componente3.GND, RE1.GND, RE2.EncoderPinC, DS1.GND, DS2.GND, Componente4.GND, U3.GND#1, U3.GND#3, ZS-042_RTC1.GND, U2.GND
  VCC: Componente1.VIN, U1.OUT+, DFPlayer_Mini1.VCC, RE1.Vcc, DS1.VDD, R2.Pin_0, R3.Pin_0, DS2.VDD, U3.VCC
  N15: Componente1.D2_PWM, Componente3.!RST
  5V: Componente1.5V, U2.+5v
  VCC_2: U1.IN+, Power_plug1.VCC, Componente2.VCC, Componente2.+, Componente4.VCC
  N16: DFPlayer_Mini1.RX, R1.Pin_1
  N17: DFPlayer_Mini1.DAC_R, U3.R2
  N18: DFPlayer_Mini1.DAC_L, U3.L2
  N19: Componente4.SPR-, SP1.+
  N20: Componente4.SPR+, SP1.-
  N21: Componente4.INL, U3.R
  N22: Componente4.AGND, U3.GND#16
  N23: Componente4.INR, U3.L

custom parts:
  LM2596 step down module: LM2596 DC-DC step down power supply module 3 A.
  DFPlayer MINI: MP3 module by DFRobot.com for playing Music from an SD-Card. Supports WAV and MP3 files.
  Digital FM Radio Receiver: Description: This is a breakout board for the Silicon Laboratories Si4703 FM tuner chip. Beyond being a simple FM radio, the Si4703 is also capable of detecting and processing both Radio Data Service (RDS) and Radio Broadcast Data Service (RBDS) information. The Si4703 even does a very good job of filtering and carrier detection. It also enables data such as the station ID and song name to be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
  KY-040 Rotary encoder: KY-040 Rotary Encoder with switch on breakout borad from AZ Delivery
  Mini Amplificador - OEP30WX2 - de Som Estéreo 2 Canais 30W + 30W: Description: A Placa Amplificador de Som 30W + 30W Estéreo é um circuito completo e ideal para quem necessita de um amplificador compacto e eficiente. De fácil instalação, conta com uma utilização mínima de componentes para melhorar as reproduções junto ao amplificador. É um módulo muito utilizado por hobistas e profissionais que necessitam de um equipamento amplificador que converta o sinal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
  Processamento de Audio - PT2314: Módulo de ajuste de qualidade de som - PT2314 Introdução do produto 1. Chip de processador de qualidade de som PT2314 integrado 2. O módulo suporta quatro conjuntos de entradas estéreo e saída de dois canais 3. O módulo suporta ajuste de volume, ajuste de agudos e graves, mudo e outras funções 4. O módulo suporta I2C ônibus para realizar todas as funções do programa 5. Luz indicadora de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
  Waterproof Pushbutton (blue): Waterproof Illuminated Pushbutton (blue)
  Nextion Display: Nextion NX8048T070_011 Display TFT Display
